# Fritzing sketch circuito-semaforo-remoto (saved by Fritzing 0.9.3b)
breadboards: 1

parts:
  U1 = ESP32-38PinWide [part_number=ESP32-38PinWide]
  J1 = Infrared Proximity Sensor
  LED1 = LED - 3mm [color="Green (560nm)" package="3 mm [THT]"]
  LED2 = LED - 3mm [color="Yellow (595nm)" package="3 mm [THT]"]
  LED3 = LED - 3mm [color="Red (633nm)" package="3 mm [THT]"]

nets:
  N1: U1.GPIO27, J1.Vout
  N2: U1.GPIO14, LED3.cathode
  N3: U1.GPIO12, LED2.cathode
  GND: U1.GND, J1.GND
  N4: U1.GPIO13, LED1.cathode
  VIN: U1.VIN, J1.Vcc, LED1.anode, LED2.anode, LED3.anode

custom parts:
  ESP32-38PinWide: Generic 38-Pin ESP32 with wide format (only access to one side of pins on a breadboard) based on Stephen Lilley's HiLetgo ESP-WROOM-32 ESP32 ESP-32S Development Board.
